# Fritzing sketch DustSensor (saved by Fritzing 0.9.3b)
breadboards: 1

parts:
  U3 = ESP32S-HiLetgo [part_number=ESP32S-HiLetgo]
  DHT3 = DHT11 Humitidy and Temperature Sensor
  U4 = Sharp Dust Sensor [part_number=GP2Y1010AU0F]
  C1 = Electrolytic Capacitor [capacitance=10µF package="100 mil [THT, electrolytic]"]
  R1 = Resistor [tolerance=±5% resistance=1k package=THT]
  o1 = Module display OLED I2C 128x64 SSD1306 [package=THT]

nets:
  N1: U3.GPIO35, U4.Vo
  GND: U3.GND, DHT3.GND, U4.LED-GND, U4.S-GND, C1.-, o1.GND
  N2: U3.GPIO13, U4.LED
  VCC: U3.VIN, DHT3.VDD, U4.VCC, R1.Pin_0, o1.VCC
  N3: U3.GPIO15, DHT3.DATA
  N4: U3.GPIO21, o1.SDA
  N5: U3.GPIO22, o1.SCL
  N6: U4.V-LED, C1.+, R1.Pin_1

notes:
  DHT11 PIN
  1 VCC
  2. Data (GPIO 15)
  3. NC
  4. GND
  GP2Y1010AU0F (L--R)
  (654321)
  1. 5V (Red)
  2. AO (GPIO35) (Black)
  3. GND (yellow)
  4. LED (GPIO13) (White)
  5. GND (Green)
  6. 5V (1K,10uF,5V) (Blue)
  SSD1306
  1. GND
  2. 5V
  3. SCL (GPIO22)
  4. SDA (GPIO21)

custom parts:
  ESP32S-HiLetgo: HiLetgo ESP-WROOM-32 ESP32 ESP-32S Development Board 2.4GHz Dual-Mode WiFi + Bluetooth Dual Cores Microcontroller The ESP32 integrated with Antenna switches, RF Balun, power amplifiers, low-noise amplifiers, filters, and management modules, and the entire solution occupies the least area of PCB. 2.4 GHz Wi-Fi plus Bluetooth dual-mode chip, with TSMC Ultra-low power consumption 40nm technology,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
  DHT11 Humitidy and Temperature Sensor: DHT11 Humidity and Temperature Sensor
  Sharp Dust Sensor: Sharp GP2Y1010AU0F Dust Sensor
  Module display OLED I2C 128x64 SSD1306: Ecran OLED I2C SSD163 de 128x64 avec connexion I2C
